// Logisim project cpu.circ as structural Verilog: 1 circuit, main circuit main
module main (
  input  [15:0] INSTRUCTION,
  input  CLOCK,
  output [15:0] FETCH_ADDRESS,
  output [15:0] s0_Value,
  output [15:0] s1_Value,
  output [15:0] s2_Value,
  output [15:0] ra_Value,
  output [15:0] sp_Value,
  output [15:0] HI_Value,
  output [15:0] LO_Value
);

  wire and_3_out, beq_equal, bnq_nequal, decoder_1_out0, decoder_1_out1, decoder_1_out2, decoder_1_out3,
       decoder_1_out4, decoder_1_out5, decoder_1_out6, decoder_1_out7, equal, i_addi, i_andi, i_beq, i_bnq,
       i_jr___jalr, i_lhalfw, i_mfl, i_mhl, i_ori, i_shalfw, i_slti, i_type, mult, not_1_out, not_2_out,
       not_3_out, or_1_out, or_2_out, or_3_out, or_5_out, or_8_out, or_9_out, R_enable, r_type, signExt,
       u_jump_link, u_lui, writeEnable;
  wire [2:0] funct, multiplexer_2_out, multiplexer_3_out, multiplexer_12_out, multiplexer_13_out, u__rd;
  wire [5:3] i_imm;
  wire [15:0] adder_1_out, adder_3_out, addres, bit_extender_1_out, bit_extender_3_out, d_LO, i_imm_SignEXT,
       main_2_result_2, MEM_p5, multiplexer_1_out, multiplexer_4_out, multiplexer_5_out, multiplexer_6_out,
       multiplexer_7_out, multiplexer_8_out, multiplexer_9_out, multiplexer_10_out, multiplexer_11_out,
       multiplexer_14_out, multiplexer_15_out, multiplexer_16_out, newPC, newPC_2, pc_2, R_RS, shifter_1_out,
       store;
  wire [15:6] INSTRUCTION_t;

  Multiplexer #(.width(16), .enable("false")) multiplexer_1 (
    .in0(addres), .in1(MEM_p5), .out(multiplexer_1_out), .sel(i_lhalfw));
  Multiplexer #(.width(3), .enable("false")) multiplexer_2 (
    .in0(i_imm), .in1(INSTRUCTION_t[11:9]), .out(multiplexer_2_out), .sel(i_type));
  Multiplexer #(.width(3), .enable("false")) multiplexer_3 (
    .in0(INSTRUCTION_t[11:9]), .in1(u__rd), .out(multiplexer_3_out), .sel(u_jump_link));
  Multiplexer #(.width(16), .enable("false")) multiplexer_4 (
    .in0(multiplexer_5_out), .in1(newPC_2), .out(multiplexer_4_out), .sel(or_1_out));
  or or_1 (or_1_out, u_jump_link, i_jr___jalr);
  Multiplexer #(.width(16), .enable("false")) multiplexer_5 (
    .in0(multiplexer_1_out), .in1(multiplexer_7_out), .out(multiplexer_5_out), .sel(or_2_out));
  // mem_main MEM: pin names not known; wires that end beside it: addres, store, i_shalfw, CLOCK, MEM_p5
  Decoder #(.select(3), .enable("false")) decoder_1 (
    .out0(decoder_1_out0), .out1(decoder_1_out1), .out2(decoder_1_out2), .out3(decoder_1_out3),
    .out4(decoder_1_out4), .out5(decoder_1_out5), .out6(decoder_1_out6), .out7(decoder_1_out7), .sel(funct));
  or or_2 (or_2_out, i_mhl, i_mfl);
  Multiplexer #(.width(16), .enable("false")) multiplexer_6 (
    .in0(addres), .in1(HI_Value), .out(multiplexer_6_out), .sel(i_mhl));
  and and_1 (R_enable, r_type, or_3_out);
  or or_3 (or_3_out, decoder_1_out0, decoder_1_out1, decoder_1_out2, decoder_1_out3, decoder_1_out4, decoder_1_out5, decoder_1_out6);
  and and_2 (mult, decoder_1_out7, r_type);
  regfile_main main_1 (
    .Read_Register_1(INSTRUCTION_t[8:6]), .Read_Register_2(multiplexer_2_out),
    .Write_Register(multiplexer_3_out), .Write_Data(multiplexer_4_out), .Write_Enable(writeEnable),
    .Clock(CLOCK), .Read_Data_1(R_RS), .Read_Data_2(store), .s0_Value(s0_Value), .s1_Value(s1_Value),
    .s2_Value(s2_Value), .ra_Value(ra_Value), .sp_Value(sp_Value));
  assign bit_extender_1_out = {{10{1'b0}}, {i_imm, funct}};  // Bit_Extender bit_extender_1
  assign i_imm_SignEXT = {{10{i_imm[5]}}, {i_imm, funct}};  // Bit_Extender bit_extender_2
  Multiplexer #(.width(16), .enable("false")) multiplexer_7 (
    .in0(multiplexer_6_out), .in1(multiplexer_8_out), .out(multiplexer_7_out), .sel(i_mfl));
  Multiplexer #(.width(16), .enable("false")) multiplexer_8 (
    .in0(addres), .in1(LO_Value), .out(multiplexer_8_out), .sel(i_mfl));
  Multiplexer #(.width(16), .enable("false")) multiplexer_9 (
    .in0(bit_extender_1_out), .in1(i_imm_SignEXT), .out(multiplexer_9_out), .sel(signExt));
  or or_4 (signExt, i_shalfw, i_lhalfw, i_slti, i_addi, i_bnq, i_beq, i_jr___jalr);
  Multiplexer #(.width(16), .enable("false")) multiplexer_10 (
    .in0(INSTRUCTION), .in1({16{1'b0}}), .out(multiplexer_10_out), .sel(or_5_out));
  or or_5 (or_5_out, i_jr___jalr, u_jump_link, beq_equal, bnq_nequal);
  Multiplexer #(.width(16), .enable("false")) multiplexer_11 (
    .in0(store), .in1(multiplexer_9_out), .out(multiplexer_11_out), .sel(and_3_out));
  and and_3 (and_3_out, i_type, not_1_out, not_2_out);
  not not_1 (not_1_out, i_bnq);
  not not_2 (not_2_out, i_beq);
  Register #(.width(16)) register_1 (
    .D(multiplexer_10_out), .Q({INSTRUCTION_t, i_imm, funct}), .clk(CLOCK));  // open: en, clr
  alu_main main_2 (
    .Switch(multiplexer_13_out), .X(R_RS), .Equal(equal), .Result(addres), .Y(multiplexer_11_out),
    .Result_2(main_2_result_2));
  Multiplexer #(.select(4), .width(3), .enable("false")) multiplexer_12 (
    .in6(3'b010), .in7(3'b110), .in8(3'b011), .in9(3'b100), .in10(3'b010), .in11(3'b010),
    .out(multiplexer_12_out), .sel(INSTRUCTION_t[15:12]));  // open: in0, in1, in2, in3, in4, in5, in12, in13, in14, in15
  or or_6 (writeEnable, R_enable, u_jump_link, i_jr___jalr, i_addi, i_slti, i_andi, i_ori, i_lhalfw, i_mhl, i_mfl);
  Multiplexer #(.width(3), .enable("false")) multiplexer_13 (
    .in0(multiplexer_12_out), .in1(funct), .out(multiplexer_13_out), .sel(r_type));
  Register #(.width(16)) u_PC_2 (.D(pc_2), .Q(newPC_2), .clk(CLOCK));  // open: en, clr
  Register #(.width(16)) HI (.D(main_2_result_2), .en(mult), .Q(HI_Value), .clk(CLOCK));  // open: clr
  or or_7 (i_type, i_jr___jalr, i_beq, i_bnq, i_addi, i_slti, i_andi, i_ori, i_lhalfw, i_shalfw, i_mhl, i_mfl);
  Register #(.width(16)) PC (.D(FETCH_ADDRESS), .Q(newPC), .clk(CLOCK));  // open: en, clr
  not not_3 (not_3_out, equal);
  and and_4 (bnq_nequal, i_bnq, not_3_out);
  or or_8 (or_8_out, bnq_nequal, beq_equal);
  and and_5 (beq_equal, equal, i_beq);
  Adder #(.width(16)) adder_1 (.a(R_RS), .b(i_imm_SignEXT), .out(adder_1_out));  // open: cin, cout
  assign bit_extender_3_out = {{6{1'b0}}, {INSTRUCTION_t[9:6], i_imm, funct}};  // Bit_Extender bit_extender_3
  Shifter #(.width(16)) shifter_1 (.in(bit_extender_3_out), .\dist (4'b0110), .out(shifter_1_out));
  Multiplexer #(.width(16), .enable("false")) multiplexer_14 (
    .in0(multiplexer_15_out), .in1({FETCH_ADDRESS[15:10], INSTRUCTION_t[9:6], i_imm, funct}),
    .out(multiplexer_14_out), .sel(u_jump_link));
  Multiplexer #(.width(16), .enable("false")) multiplexer_15 (
    .in0(multiplexer_16_out), .in1(adder_3_out), .out(multiplexer_15_out), .sel(or_8_out));
  Multiplexer #(.width(16), .enable("false")) multiplexer_16 (
    .in0(pc_2), .in1(adder_1_out), .out(multiplexer_16_out), .sel(i_jr___jalr));
  or or_9 (or_9_out, mult, u_lui);
  Multiplexer #(.width(16), .enable("false")) multiplexer_17 (
    .in0(addres), .in1(shifter_1_out), .out(d_LO), .sel(u_lui));
  Register #(.width(16)) u_PC_2_dup2 (.D(multiplexer_14_out), .en(1'b1), .Q(FETCH_ADDRESS), .clk(CLOCK));  // open: clr
  assign u__rd = {{1{1'b0}}, INSTRUCTION_t[11:10]};  // Bit_Extender bit_extender_4
  Register #(.width(16)) LO (.D(d_LO), .en(or_9_out), .Q(LO_Value), .clk(CLOCK));  // open: clr
  Adder #(.width(16)) adder_2 (.a(FETCH_ADDRESS), .b(16'h2), .out(pc_2));  // open: cin, cout
  Adder #(.width(16)) adder_3 (.a(newPC), .b(i_imm_SignEXT), .out(adder_3_out));  // open: cin, cout
  Decoder #(.select(4), .enable("false")) decoder_2 (
    .out0(r_type), .out1(u_lui), .out2(u_jump_link), .out3(i_jr___jalr), .out4(i_beq), .out5(i_bnq),
    .out6(i_addi), .out7(i_slti), .out8(i_andi), .out9(i_ori), .out10(i_lhalfw), .out11(i_shalfw),
    .out12(i_mhl), .out13(i_mfl), .sel(INSTRUCTION_t[15:12]));  // open: out14, out15

  // Other names for the same wires on the sheet: clk = CLOCK; fetch_addr[15:0] = FETCH_ADDRESS;
  //   PC[15:0] = FETCH_ADDRESS; HI[15:0] = HI_Value; rd[2:0] = INSTRUCTION_t[11:9];
  //   opcode[3:0] = INSTRUCTION_t[15:12]; i_imm[2:0] = funct; INSTRUCTION_t[5:0] = {i_imm, funct};
  //   jumpAddress[15:0] = {FETCH_ADDRESS[15:10], INSTRUCTION_t[9:6], i_imm, funct};
  //   u_imm[9:0] = {INSTRUCTION_t[9:6], i_imm, funct}; rt[2:0] = i_imm; rs[2:0] = INSTRUCTION_t[8:6];
  //   pc_bits_10_15[5:0] = FETCH_ADDRESS[15:10]; LO[15:0] = LO_Value; ra[15:0] = ra_Value; s0[15:0] = s0_Value;
  //   s1[15:0] = s1_Value; s2[15:0] = s2_Value; sp[15:0] = sp_Value; writeBack[15:0] = addres

  // Notes on the sheet:
  //   Output
  //   These are outputs/inputs from run.circ
  //   Inputs
  //   These are DEBUG/TEST outputs from your circuit.
endmodule
