// Logisim project regfile.circ as structural Verilog: 1 circuit, main circuit main
module main (
  input  [2:0] Read_Register_1,
  input  [2:0] Read_Register_2,
  input  [2:0] Write_Register,
  input  [15:0] Write_Data,
  input  Write_Enable,
  input  Clock,
  output [15:0] s0_Value,
  output [15:0] s1_Value,
  output [15:0] s2_Value,
  output [15:0] ra_Value,
  output [15:0] sp_Value,
  output [15:0] Read_Data_1,
  output [15:0] Read_Data_2
);

  wire _0, _1, _2, _3, _4, _5, _6, _7;
  wire [15:0] _0_q, a0, v0;

  Register #(.width(16)) u__0 (.D(Write_Data), .en(_0), .Q(_0_q), .clk(Clock), .clr(1'b1));
  Register #(.width(16)) ra (.D(Write_Data), .en(_1), .Q(ra_Value), .clk(Clock));  // open: clr
  Register #(.width(16)) s0 (.D(Write_Data), .en(_2), .Q(s0_Value), .clk(Clock));  // open: clr
  Register #(.width(16)) s1 (.D(Write_Data), .en(_3), .Q(s1_Value), .clk(Clock));  // open: clr
  Register #(.width(16)) s2 (.D(Write_Data), .en(_4), .Q(s2_Value), .clk(Clock));  // open: clr
  Register #(.width(16)) u_a0 (.D(Write_Data), .en(_5), .Q(a0), .clk(Clock));  // open: clr
  Register #(.width(16)) u_v0 (.D(Write_Data), .en(_6), .Q(v0), .clk(Clock));  // open: clr
  Register #(.width(16)) sp (.D(Write_Data), .en(_7), .Q(sp_Value), .clk(Clock));  // open: clr
  Multiplexer #(.select(3), .width(16)) multiplexer_1 (
    .in0(_0_q), .in1(ra_Value), .in2(s0_Value), .in3(s1_Value), .in4(s2_Value), .in5(a0), .in6(v0),
    .in7(sp_Value), .out(Read_Data_1), .sel(Read_Register_1));  // open: en
  Demultiplexer #(.select(3)) demultiplexer_1 (
    .out0(_0), .out1(_1), .out2(_2), .out3(_3), .out4(_4), .out5(_5), .out6(_6), .out7(_7),
    .in(Write_Enable), .sel(Write_Register));  // open: en
  Multiplexer #(.select(3), .width(16)) multiplexer_2 (
    .in0(_0_q), .in1(ra_Value), .in2(s0_Value), .in3(s1_Value), .in4(s2_Value), .in5(a0), .in6(v0),
    .in7(sp_Value), .out(Read_Data_2), .sel(Read_Register_2));  // open: en

  // Other names for the same wires on the sheet: clk = Clock; ra[15:0] = ra_Value; read_data1[15:0] = Read_Data_1;
  //   read_data2[15:0] = Read_Data_2; read_reg1[2:0] = Read_Register_1; read_reg2[2:0] = Read_Register_2;
  //   s0[15:0] = s0_Value; s1[15:0] = s1_Value; s2[15:0] = s2_Value; sp[15:0] = sp_Value; write_en = Write_Enable;
  //   write_reg[2:0] = Write_Register

  // Notes on the sheet:
  //   INPUTS to your circuit
  //   DON'T CHANGE THE LOCATIONS OF THE INPUTS AND OUTPUTS!
  //   These are DEBUG/TEST outputs from your circuit.
  //   OUTPUTS from your circuit
endmodule
